# Fritzing sketch pcb (saved by Fritzing 0.9.3b)
circuit board: 10.5cm x 6cm
breadboards: 1

parts:
  Q1 = Basic FET N-Channel [package="TO220 [THT]"]
  SSR0 = OMRON G3MB-202p [package=relay-s108t02]
  T0 = NPN-Transistor [package="TO92 [THT]"]
  U4 = LuaNode32 / ESP32 [part_number="ESP32 LuaNode32"]
  R1 = Resistor [tolerance=±5% resistance=4.7k package="2010 [SMD]"]
  SSR_IN = Header 2 [part_number=SSR_IN package=screwterminal-3.5mm-2_lock]
  SSR0_OUT = Header 2 [part_number=SSR0 package=screwterminal-3.5mm-2_lock]
  C2 = Electrolytic Capacitor [capacitance=1000µF package="200 mil [THT, electrolytic]"]
  SSR1 = OMRON G3MB-202p [package=relay-s108t02]
  T1 = NPN-Transistor [package="TO92 [THT]"]
  R2 = Resistor [tolerance=±5% resistance=4.7k package="2010 [SMD]"]
  SSR1_OUT = Header 2 [part_number=SSR1 package=screwterminal-3.5mm-2_lock]
  SSR2 = OMRON G3MB-202p [package=relay-s108t02]
  T2 = NPN-Transistor [package="TO92 [THT]"]
  R3 = Resistor [tolerance=±5% resistance=4.7k package="2010 [SMD]"]
  SSR2_OUT = Header 2 [part_number=SSR2 package=screwterminal-3.5mm-2_lock]
  R4 = Resistor [tolerance=±5% resistance=1k package="2010 [SMD]"]
  R5 = Resistor [tolerance=±5% resistance=10k package="2010 [SMD]"]
  Q7 = Basic FET N-Channel [package="TO220 [THT]"]
  R6 = Resistor [tolerance=±5% resistance=10k package="2010 [SMD]"]
  R7 = Resistor [tolerance=±5% resistance=1k package="2010 [SMD]"]
  R8 = Resistor [tolerance=±5% resistance=150 package="2010 [SMD]"]
  LED4 = LEDs [package=led-1206]
  LED5 = LEDs [package=led-1206]
  R9 = Resistor [tolerance=±5% resistance=150 package="2010 [SMD]"]
  LED6 = LEDs [package=led-1206]
  R10 = Resistor [tolerance=±5% resistance=150 package="2010 [SMD]"]
  MPC = Mini-360 DC-DC Buck converter [package=THT]
  J1 = female pin header, 2 pins [form="♀ (female)"]
  J2 = female pin header, 2 pins [form="♀ (female)"]
  J3 = female pin header, 2 pins [form="♀ (female)"]
  ANALOG0 = female pin header, 2 pins [form="♀ (female)"]
  ANALOG1 = female pin header, 2 pins [form="♀ (female)"]
  DHT22 = female pin header, 3 pins [form="♀ (female)"]
  R12 = Resistor [tolerance=±5% resistance=10k package="2010 [SMD]"]
  I2C = female pin header, 4 pins [form="♀ (female)"]
  I2C1 = female pin header, 4 pins [form="♀ (female)"]
  I2C2 = female pin header, 4 pins [form="♀ (female)"]
  I2C3 = female pin header, 4 pins [form="♀ (female)"]
  ENCODER = female pin header, 4 pins [form="♀ (female)"]
  PWM1 = female pin header, 2 pins [form="♀ (female)"]
  PWM0 = female pin header, 2 pins [form="♀ (female)"]
  J4 = female pin header, 2 pins [form="♀ (female)"]
  J5 = female pin header, 2 pins [form="♀ (female)"]

nets:
  N1: Q1.gate, R4.Pin_0, R5.Pin_0
  N2: Q1.drain, PWM0.pin2
  N3: Q1.source, T0.E, U4.GND, C2.-, T1.E, T2.E, R5.Pin_1, Q7.source, R6.Pin_1, MPC.OUT-, DHT22.pin3, R12.Pin_0, I2C.pin3, I2C1.pin3, I2C2.pin3, I2C3.pin3, ENCODER.pin4
  N4: SSR0.T1, SSR0_OUT.2
  N5: SSR0.T2, SSR_IN.2, SSR1.T2, SSR2.T2
  N6: SSR0.+, SSR1.+, SSR2.+, R8.Pin_0, R9.Pin_0, R10.Pin_0
  N7: SSR0.-, T0.C, LED4.C
  N8: T0.B, R1.Pin_1
  N9: U4.D34, DHT22.pin2, R12.Pin_1
  N10: U4.D35, ANALOG0.pin1
  N11: U4.D32, ANALOG1.pin1
  N12: U4.D12, R7.Pin_1
  N13: U4.D13, R4.Pin_1
  N14: U4.Vin, MPC.OUT+
  N15: U4.3V3, C2.+, ANALOG0.pin2, ANALOG1.pin2, DHT22.pin1, I2C.pin4, I2C1.pin4, I2C2.pin4, I2C3.pin4
  N16: U4.D15, R3.Pin_0
  N17: U4.D2, R2.Pin_0
  N18: U4.D4, R1.Pin_0
  N19: U4.D5, ENCODER.pin3
  N20: U4.D18, ENCODER.pin2
  N21: U4.D19, ENCODER.pin1
  N22: U4.D21, I2C.pin2, I2C1.pin2, I2C2.pin2, I2C3.pin2
  N23: U4.D22, I2C.pin1, I2C1.pin1, I2C2.pin1, I2C3.pin1
  N24: SSR_IN.1, SSR0_OUT.1, SSR1_OUT.1, SSR2_OUT.1
  N25: SSR1.T1, SSR1_OUT.2
  N26: SSR1.-, T1.C, LED5.C
  N27: T1.B, R2.Pin_1
  N28: SSR2.T1, SSR2_OUT.2
  N29: SSR2.-, T2.C, LED6.C
  N30: T2.B, R3.Pin_1
  N31: Q7.gate, R6.Pin_0, R7.Pin_0
  N32: Q7.drain, PWM1.pin2
  N33: R8.Pin_1, LED4.A
  N34: LED5.A, R9.Pin_1
  N35: LED6.A, R10.Pin_1
  N36: MPC.IN-, J1.pin2, J2.pin2, J3.pin2, J4.pin2, J5.pin2
  N37: MPC.IN+, J1.pin1, J2.pin1, J3.pin1, PWM1.pin1, PWM0.pin1, J4.pin1, J5.pin1

notes:
  Terrarium Controller v0.1

custom parts:
  OMRON G3MB-202p: SPST SS relay
  LuaNode32 / ESP32: ESP32 based LuaNode32
  Mini-360 DC-DC Buck converter: Mini-360 DC-DC Buck converter. Tiny buck step down voltage converter, input voltage 4.75 to 23V output 1 to 17V adjustable. Available from ebay and the like.
