# Fritzing sketch pcb0_3 (saved by Fritzing 0.9.3b)
circuit board: 10.5cm x 6cm
breadboards: 1

parts:
  LED4 = LEDs [package=led-1206]
  SSR0_OUT = screw terminal, 2 pins
  F3 = Resettable Fuse PTC [package=ptc]
  F4 = Resettable Fuse PTC [package=ptc]
  ENCODER = female pin header, 4 pins [form="♀ (female)"]
  SSR1_OUT = screw terminal, 2 pins
  SSR2_OUT = screw terminal, 2 pins
  F5 = Resettable Fuse PTC [package=ptc]
  SSR0 = OMRON G3MB-202p [package=relay-s108t02]
  +12V- = female pin header, 2 pins [form="♀ (female)"]
  I2C2 = female pin header, 4 pins [form="♀ (female)"]
  T2 = NPN-Transistor [package="SOT-23 [SMD]"]
  MPC = Mini-360 DC-DC Buck converter [package=THT]
  Q7 = Basic FET N-Channel [package="TO220 [THT]"]
  J2 = female pin header, 2 pins [form="♀ (female)"]
  LED6 = LEDs [package=led-1206]
  J4 = female pin header, 2 pins [form="♀ (female)"]
  SSR1 = OMRON G3MB-202p [package=relay-s108t02]
  I2C3 = female pin header, 4 pins [form="♀ (female)"]
  C2 = Electrolytic Capacitor [capacitance=1000µF package="200 mil [THT, electrolytic]"]
  SSR_IN = screw terminal, 2 pins
  T0 = NPN-Transistor [package="SOT-23 [SMD]"]
  LED5 = LEDs [package=led-1206]
  PWM0 = female pin header, 2 pins [form="♀ (female)"]
  J5 = female pin header, 2 pins [form="♀ (female)"]
  I2C = female pin header, 4 pins [form="♀ (female)"]
  I2C1 = female pin header, 4 pins [form="♀ (female)"]
  J3 = female pin header, 2 pins [form="♀ (female)"]
  T1 = NPN-Transistor [package="SOT-23 [SMD]"]
  DHT22 = female pin header, 3 pins [form="♀ (female)"]
  PWM1 = female pin header, 2 pins [form="♀ (female)"]
  Q1 = Basic FET N-Channel [package="TO220 [THT]"]
  R13 = Resistor [tolerance=±5% resistance=10k package="1206 [SMD]"]
  R1 = Resistor [tolerance=±5% resistance=10k package="1206 [SMD]"]
  R14 = Resistor [tolerance=±5% resistance=10k package="1206 [SMD]"]
  R2 = Resistor [tolerance=±5% resistance=10k package="1206 [SMD]"]
  R15 = Resistor [tolerance=±5% resistance=10k package="1206 [SMD]"]
  R3 = Resistor [tolerance=±5% resistance=10k package="1206 [SMD]"]
  R10 = Resistor [tolerance=±5% resistance=220 package="1206 [SMD]"]
  R9 = Resistor [tolerance=±5% resistance=220 package="1206 [SMD]"]
  R8 = Resistor [tolerance=±5% resistance=220 package="1206 [SMD]"]
  R4 = Resistor [tolerance=±5% resistance=1k package="1206 [SMD]"]
  R6 = Resistor [tolerance=±5% resistance=10k package="1206 [SMD]"]
  R7 = Resistor [tolerance=±5% resistance=1k package="1206 [SMD]"]
  R12 = Resistor [tolerance=±5% resistance=10k package="1206 [SMD]"]
  R5 = Resistor [tolerance=±5% resistance=10k package="1206 [SMD]"]
  SSR2 = OMRON G3MB-202p [package=relay-s108t02]
  IC1 = Voltage Regulator AMS1117 [package=sot223]
  A1 = female pin header, 3 pins [form="♀ (female)"]
  A0 = female pin header, 3 pins [form="♀ (female)"]
  Bauteil1 = ESP-WROOM-32 [ESP-32S] Module [part_number=ESP-WROOM-32]
  C3 = Tantalum Capacitor [capacitance=22µF package="A 3216 [SMD, tantalum]"]

nets:
  N1: LED4.A, R8.Pin_1
  N2: LED4.C, SSR0.-, T0.1
  N3: SSR0_OUT.pin1, SSR1_OUT.pin1, SSR2_OUT.pin1, SSR_IN.pin1
  N4: SSR0_OUT.pin2, F3.1
  N5: F3.2, SSR0.T1
  N6: F4.1, SSR1_OUT.pin2
  N7: F4.2, SSR1.T1
  N8: ENCODER.pin1, Bauteil1.IO19
  N9: ENCODER.pin2, Bauteil1.IO18
  N10: ENCODER.pin3, Bauteil1.IO5
  N11: ENCODER.pin4, I2C2.pin3, T2.2, MPC.OUT-, Q7.source, I2C3.pin3, C2.-, T0.2, I2C.pin3, I2C1.pin3, T1.2, DHT22.pin3, Q1.source, R13.Pin_0, R14.Pin_0, R15.Pin_0, R6.Pin_1, R12.Pin_0, R5.Pin_1, IC1.GND, A0.pin2, Bauteil1.IO2, Bauteil1.RST, C3.-
  N12: SSR2_OUT.pin2, F5.1
  N13: F5.2, SSR2.T1
  N14: SSR0.T2, SSR1.T2, SSR_IN.pin2, SSR2.T2
  N15: SSR0.+, SSR1.+, C2.+, R10.Pin_0, R9.Pin_0, R8.Pin_0, SSR2.+
  N16: +12V-.pin1, MPC.IN+, J2.pin1, J4.pin1, PWM0.pin1, J5.pin1, J3.pin1, PWM1.pin1
  N17: +12V-.pin2, MPC.IN-, J2.pin2, J4.pin2, J5.pin2, J3.pin2
  N18: I2C2.pin1, I2C3.pin1, I2C.pin1, I2C1.pin1, Bauteil1.IO22
  N19: I2C2.pin2, I2C3.pin2, I2C.pin2, I2C1.pin2, Bauteil1.IO21
  N20: I2C2.pin4, I2C3.pin4, I2C.pin4, I2C1.pin4, DHT22.pin1, IC1.OUT, A1.pin3, A0.pin3, Bauteil1.3V3, C3.+
  N21: T2.0, R15.Pin_1, R3.Pin_1
  N22: T2.1, LED6.C, SSR2.-
  N23: MPC.OUT+, IC1.IN
  N24: Q7.gate, R6.Pin_0, R7.Pin_0
  N25: Q7.drain, PWM1.pin2
  N26: LED6.A, R10.Pin_1
  N27: SSR1.-, LED5.C, T1.1
  N28: T0.0, R13.Pin_1, R1.Pin_1
  N29: LED5.A, R9.Pin_1
  N30: PWM0.pin2, Q1.drain
  N31: T1.0, R14.Pin_1, R2.Pin_1
  N32: DHT22.pin2, R12.Pin_1, Bauteil1.IO4
  N33: Q1.gate, R4.Pin_0, R5.Pin_0
  N34: R1.Pin_0, Bauteil1.IO26
  N35: R2.Pin_0, Bauteil1.IO27
  N36: R3.Pin_0, Bauteil1.IO14
  N37: R4.Pin_1, Bauteil1.IO13
  N38: R7.Pin_1, Bauteil1.IO12
  N39: A1.pin1, A0.pin1, Bauteil1.GND
  N40: A1.pin2, Bauteil1.IO15

notes:
  Terrarium Controller v0.2
  VCC
  GND
  SDA
  SCL

custom parts:
  OMRON G3MB-202p: SPST SS relay
  Mini-360 DC-DC Buck converter: Mini-360 DC-DC Buck converter. Tiny buck step down voltage converter, input voltage 4.75 to 23V output 1 to 17V adjustable. Available from ebay and the like.
  ESP-WROOM-32 [ESP-32S] Module: Espressif ESP-WROOM-32 WiFi/Bluetooth LE microcontroller module also known as the Ai-Thinker ESP-32S module with similar formfactor. The ESP32 is a microcontroller chip with WiFi and BLE capabilities. The chip is developed by Espressif and is the successor to the popular ESP8266 WiFi module.
